# Fritzing sketch ATtiny84 programmer micro (saved by Fritzing 0.9.6b)
breadboards: 1

parts:
  Part2 = Arduino Micro (Rev3)  # not connected
  U1 = IC, DIP package, 14 pins [chip_label=ATTINY84A]
  C1 = Electrolytic Capacitor [capacitance=10µF voltage=35V package="0807 [SMD, electrolytic]"]
  R1 = Resistor [tolerance=±5% resistance=150 package="0402 [SMD]"]
  LED1 = LED - 5mm [color="Red (633nm)" current=0.030 package="5 mm [THT]"]

nets:
  N1: U1.pin13, R1.Pin_0
  N2: U1.pin14, C1.-, LED1.cathode
  N3: R1.Pin_1, LED1.anode

notes:
  Remember to upload the ArduinoISP sketch before the capcitor goes onto the reset pin or you won't be able to programme it!
