# Fritzing sketch ATtiny84 programmer (saved by Fritzing 0.9.6b)
stripboards: 1

parts:
  Part1 = Arduino Uno (Rev3) - ICSP
  U1 = IC, SIP package, 7 pins [chip_label=ATTINY84A]
  C1 = Electrolytic Capacitor [capacitance=10µF package="0807 [SMD, electrolytic]"]
  J1 = male pin header, 5 pins [form="♂ (male)"]
  J2 = male pin header, 3 pins [form="♂ (male)"]

nets:
  N1: Part1.GND, C1.-, J1.pin1
  N2: U1.pin1, J2.pin3
  N3: U1.pin4, J1.pin5
  N4: U1.pin7, J1.pin4
  N5: C1.+, J2.pin1

notes:
  Reset | | 5V
  GND 13 12 11 10
  Current programmer doesn't have this Capacitor and looks like I may have removed it. Seems to work with no ill effects
