# Fritzing sketch ATTinyRGBdimmer (saved by Fritzing 0.9.6b)
breadboards: 1

parts:
  IC1 = IC, DIP package, 14 pins [chip_label=ATTINY84A]
  LED1 = RGB LED - (4 legs) [package="5 mm [THT]"]
  C3 = Ceramic Capacitor [capacitance=100nF package="100 mil [THT, multilayer]"]
  R1 = Resistor [tolerance=±5% power=0.25 resistance=150 package=THT]
  R2 = Resistor [tolerance=±5% power=0.25 resistance=150 package=THT]
  R3 = Resistor [tolerance=±5% power=0.25 resistance=100 package=THT]
  X1 = USB Connectors [package=usb-b-smt]
  R4 = Rotary Potentiometer (Small) [maximum_resistance=100kΩ package=THT]

nets:
  N1: IC1.pin1, LED1.common_anode, C3.0, X1.VBUS, R4.leg2
  N2: IC1.pin5, R3.Pin_1
  N3: IC1.pin6, R2.Pin_1
  N4: IC1.pin7, R1.Pin_1
  N5: IC1.pin13, R4.wiper
  N6: IC1.pin14, C3.1, X1.GND, R4.leg1
  N7: LED1.red_cathode, R1.Pin_0
  N8: LED1.green_cathode, R2.Pin_0
  N9: LED1.blue_cathode, R3.Pin_0

notes:
  Common anode RGB
  100nF capacitor (marked 104)
