# Fritzing sketch ATTinyRGBdimmerStrip (saved by Fritzing 0.9.6b)
stripboards: 1

parts:
  C4 = Ceramic Capacitor [capacitance=100nF voltage=35V package="100 mil [THT, multilayer]"]
  LED2 = RGB LED - (4 legs) [package="5 mm [THT]"]
  R1 = Resistor [tolerance=±5% resistance=150 power=0.25 package=THT]
  R2 = Resistor [tolerance=±5% resistance=100 power=0.25 package=THT]
  R3 = Resistor [tolerance=±5% resistance=150 power=0.25 package=THT]
  U4 = POT [package=alps_pot]
  X2 = USB Connectors [package=usb-b-smt]
  IC2 = IC, DIP package, 14 pins [chip_label=ATTINY84A]

nets:
  N1: C4.0, LED2.common_anode, U4.A, X2.VBUS, IC2.pin1
  N2: C4.1, U4.E, X2.GND, IC2.pin14
  N3: LED2.red_cathode, R3.Pin_1
  N4: LED2.green_cathode, R1.Pin_1
  N5: LED2.blue_cathode, R2.Pin_1
  N6: R1.Pin_0, IC2.pin6
  N7: R2.Pin_0, IC2.pin5
  N8: R3.Pin_0, IC2.pin7
  N9: U4.S, IC2.pin13

notes:
  Common anode RGB
  100nF capacitor (marked 104)
  REMEMBER to cut traces behind IC and below LED
